// Logisim project 332_pipelined.circ as structural Verilog: 4 circuits, main circuit main
module main (
  input  [7:0] in_1,
  input  in_2,
  output [3:0] oppcode,
  output [1:0] rs,
  output [1:0] rt,
  output [1:0] rd,
  output I_f_flag,
  output R_f_flag,
  output [9:0] RS_Data,
  output [9:0] RT_Data,
  output [9:0] RD_Data,
  output [9:0] ALU_out,
  output [9:0] mem_data
);

  wire Clk, L_S_flag, WR_flag;
  wire [1:0] I_format, R_opp;
  wire [7:0] adder_1_out, PC_q;
  wire [9:0] Address, IM;

  Clock Clock (.out(Clk));
  Register PC (.D(adder_1_out), .en(in_2), .Q(PC_q), .clk(Clk));  // open: clr
  Adder adder_1 (.a(PC_q), .b(in_1), .out(adder_1_out));  // open: cin, cout
  ROM #(.dataWidth(10)) rom_1 (.addr(PC_q), .data({oppcode, rs, rt, rd}), .sel(in_2));
  RAM #(.addrWidth(10), .dataWidth(10)) ram_1 (.addr(Address), .data(mem_data), .ld(L_S_flag));  // open: sel, clk, clr
  Control control_1 (
    .oppcode(oppcode), .Format_F(I_f_flag), .R_format(R_opp), .i_format(I_format), .L_S_flag(L_S_flag),
    .Write_Reg_Flag(WR_flag));
  assign IM = {{8{1'b0}}, rd};  // Bit_Extender bit_extender_1
  Multiplexer #(.width(10), .enable("false")) multiplexer_1 (
    .in0(ALU_out), .in1(mem_data), .out(RD_Data), .sel(L_S_flag));
  not not_1 (R_f_flag, I_f_flag);
  Register_FIle register_file_1 (
    .Write_Reg(rd), .Write_Data(RD_Data), .Ven_EN(WR_flag), .Clock(Clk), .Read_Data1(RS_Data),
    .Read_Reg1(rs), .Read_Data_2(RT_Data), .Read_Reg2(rt));
  ALU alu_1 (.RS(RS_Data), .RT(RT_Data), .Select_Opperation(R_opp), .OUTPUT(ALU_out));  // open: Cin, Cout
  assign Address = {{8{1'b0}}, rt};  // Bit_Extender bit_extender_2

  // Other names for the same wires on the sheet: opp_C[3:0] = oppcode; en = in_2; Fflg = I_f_flag; RDd[9:0] = RD_Data;
  //   RSd[9:0] = RS_Data; RTd[9:0] = RT_Data

  // Notes on the sheet:
  //   instruction mem
  //   1.oppcode, 2. rs, 3.rt, 4.rd
  //   Data mem
  //   contents of rom_1 (hex, n*v repeats v):
  //   6*0 6 204 204 200 a0 1c6 86 85 16*86 280 0 0 b0 0 83
endmodule

// REG FILE
module Register_FIle (
  input  [9:0] Write_Data,
  input  [1:0] Write_Reg,
  input  Ven_EN,
  input  Clock,
  input  [1:0] Read_Reg1,
  input  [1:0] Read_Reg2,
  output [9:0] Read_Data1,
  output [9:0] Read_Data_2
);

  wire R1, R2, R3, R4;
  wire [9:0] Dout1, Dout2, Dout3, Dout4;

  Decoder #(.select(2)) decoder_1 (.out0(R1), .out1(R2), .out2(R4), .out3(R3), .sel(Write_Reg), .en(Ven_EN));
  Register #(.width(10)) u_R1 (.D(Write_Data), .en(R1), .Q(Dout1), .clk(Clock));  // open: clr
  Register #(.width(10)) u_R3 (.D(Write_Data), .en(R3), .Q(Dout3), .clk(Clock));  // open: clr
  Register #(.width(10)) u_R2 (.D(Write_Data), .en(R2), .Q(Dout2), .clk(Clock));  // open: clr
  Register #(.width(10)) u_R4 (.D(Write_Data), .en(R4), .Q(Dout4), .clk(Clock));  // open: clr
  Multiplexer #(.select(2), .width(10), .enable("false")) multiplexer_1 (
    .in0(Dout1), .in1(Dout2), .in2(Dout4), .in3(Dout3), .out(Read_Data1), .sel(Read_Reg1));
  Multiplexer #(.select(2), .width(10), .enable("false")) multiplexer_2 (
    .in0(Dout1), .in1(Dout2), .in2(Dout4), .in3(Dout3), .out(Read_Data_2), .sel(Read_Reg2));

  // Other names for the same wires on the sheet: clk = Clock; Din[9:0] = Write_Data; do1[9:0] = Read_Data1;
  //   do2[9:0] = Read_Data_2; en = Ven_EN; RD1[1:0] = Read_Reg1; RD2[1:0] = Read_Reg2; writeReg[1:0] = Write_Reg
endmodule

module ALU (
  input  [1:0] Select_Opperation,
  input  Cin,
  input  [9:0] RS,
  input  [9:0] RT,
  output Cout,
  output [9:0] OUTPUT
);

  wire [9:0] Add, And, Or, Sub;

  assign And = RS & RT;  // AND_Gate and_1, 10 bits wide
  assign Or = RS | RT;  // OR_Gate or_1, 10 bits wide
  Adder #(.width(10)) adder_1 (.a(RS), .b(RT), .out(Add), .cin(Cin), .cout(Cout));
  Subtractor #(.width(10)) subtractor_1 (.a(RS), .b(RT), .out(Sub), .bin(Cin), .bout(Cout));
  Multiplexer #(.select(2), .width(10), .enable("false")) multiplexer_1 (
    .in0(And), .in1(Or), .in2(Add), .in3(Sub), .out(OUTPUT), .sel(Select_Opperation));

  // Other names for the same wires on the sheet: mIn[1:0] = Select_Opperation; Result[9:0] = OUTPUT; RSin[9:0] = RS;
  //   RTin[9:0] = RT
endmodule

// Format Detector
module Control (
  input  [3:0] oppcode,
  output [1:0] R_format,
  output Write_Reg_Flag,
  output Format_F,
  output [1:0] i_format,
  output L_S_flag
);

  wire R;

  Multiplexer multiplexer_1 (.in0(1'b0), .in1(1'b1), .out(Format_F), .sel(oppcode[3]));  // open: en
  not not_1 (R, Format_F);
  Multiplexer #(.select(2), .width(2)) multiplexer_2 (
    .in0(2'b00), .in1(2'b01), .in2(2'b10), .in3(2'b11), .out(R_format), .sel(oppcode[1:0]), .en(R));
  Multiplexer #(.select(2), .width(2)) multiplexer_3 (
    .in0(2'b00), .in1(2'b01), .in2(2'b10), .in3(2'b11), .out(i_format), .sel(oppcode[1:0]), .en(Format_F));
  Multiplexer #(.select(4)) multiplexer_4 (
    .in0(1'b0), .in1(1'b0), .in2(1'b0), .in3(1'b0), .in4(1'b0), .in5(1'b0), .in6(1'b0), .in7(1'b0),
    .in8(1'b1), .in9(1'b0), .in10(1'b1), .in11(1'b0), .in12(1'b0), .in13(1'b0), .in14(1'b0), .in15(1'b0),
    .out(L_S_flag), .sel(oppcode));  // open: en
  Multiplexer #(.select(4)) multiplexer_5 (
    .in0(1'b1), .in1(1'b1), .in2(1'b1), .in3(1'b1), .in8(1'b1), .in9(1'b0), .in10(1'b1),
    .out(Write_Reg_Flag), .sel(oppcode));  // open: in4, in5, in6, in7, in11, in12, in13, in14, in15, en

  // Other names for the same wires on the sheet: I = Format_F; opp[1:0] = oppcode[1:0]; oppC[3:0] = oppcode;
  //   format = oppcode[3]

  // Notes on the sheet:
  //   it will check for type and will give  0 for r format, 1 for I format
endmodule
